// Logisim project LAB1_Basic_functions.circ as structural Verilog: 1 circuit, main circuit main
module main (
  input  in_1,
  input  in_2,
  input  in_3,
  input  in_4,
  input  in_5,
  input  in_6,
  input  in_7,
  input  in_8,
  input  in_9,
  input  in_10,
  input  in_11,
  input  in_12,
  input  in_13,
  input  in_14,
  input  A,
  input  A_2,
  input  B,
  input  B_2,
  input  C,
  input  C_2,
  output out_21,
  output out_22,
  output out_23,
  output out_24,
  output out_25,
  output out_26,
  output out_27,
  output out_28,
  output out_29,
  output out_30
);

  wire and_1_out, nand_1_out, nand_3_out, nand_4_out, nand_5_out, nand_7_out, nand_8_out, nand_10_out,
       nand_12_out, nand_13_out, nand_14_out, nand_15_out, nand_16_out, nand_17_out, nand_18_out,
       nand_19_out, nand_20_out, nand_21_out, nor_1_out, nor_2_out, nor_3_out, nor_4_out, nor_6_out,
       nor_9_out, nor_10_out, xor_1_out;

  nand nand_1 (nand_1_out, in_11, in_11);
  nand nand_2 (out_22, in_2, in_2);
  nand nand_3 (nand_3_out, in_4, in_6);
  nand nand_4 (nand_4_out, in_8, in_8);
  nand nand_5 (nand_5_out, in_9, in_9);
  nand nand_6 (out_24, nand_3_out, nand_3_out);
  nand nand_7 (nand_7_out, nand_1_out, in_14);
  nand nand_8 (nand_8_out, in_14, in_14);
  nand nand_9 (out_26, nand_4_out, nand_5_out);
  nand nand_10 (nand_10_out, nand_8_out, in_11);
  xor xor_1 (xor_1_out, A_2, B_2);
  and and_1 (and_1_out, C_2, B_2, A_2);
  nand nand_11 (out_28, nand_7_out, nand_10_out);
  or or_1 (out_29, xor_1_out, C_2, and_1_out);
  nor nor_1 (nor_1_out, in_12, in_12);
  nor nor_2 (nor_2_out, in_3, in_5);
  nor nor_3 (nor_3_out, in_7, in_7);
  nor nor_4 (nor_4_out, in_10, in_10);
  nor nor_5 (out_21, in_1, in_1);
  nor nor_6 (nor_6_out, in_13, in_13);
  nor nor_7 (out_23, nor_2_out, nor_2_out);
  nor nor_8 (out_25, nor_3_out, nor_4_out);
  nor nor_9 (nor_9_out, nor_1_out, nor_6_out);
  nand nand_12 (nand_12_out, A, B, C);
  nand nand_13 (nand_13_out, A, A);
  nor nor_10 (nor_10_out, in_13, in_12);
  nand nand_14 (nand_14_out, nand_12_out, nand_12_out);
  nor nor_11 (out_27, nor_9_out, nor_10_out);
  nand nand_15 (nand_15_out, nand_13_out, B);
  nand nand_16 (nand_16_out, B, B);
  nand nand_17 (nand_17_out, nand_16_out, A);
  nand nand_18 (nand_18_out, nand_15_out, nand_17_out);
  nand nand_19 (nand_19_out, nand_14_out, nand_14_out);
  nand nand_20 (nand_20_out, nand_18_out, nand_18_out);
  nand nand_21 (nand_21_out, C, C);
  nand nand_22 (out_30, nand_19_out, nand_20_out, nand_21_out);

  // Notes on the sheet:
  //   NAND Gates (AND Gates)
  //   NAND Gates (OR Gates)
  //   NAND Gates (XOR Gates)
  //   NAND Gates (NOT Gates)
  //   y = a*b*c + a^b + c
  //   NOR Gates (NOT Gates)
  //   NOR Gates (OR Gates)
  //   NOR (AND Gates)
  //   NOR Gates (XOR Gates)
  //   y = a*b*c + a^b + c
endmodule
