// Logisim project SYC_03_s21353.circ as structural Verilog
// 4 bit adder
module Task_4 (
  input  B0,
  input  B1,
  input  B2,
  input  B3,
  input  A0,
  input  A1,
  input  A2,
  input  A3,
  output x0,
  output x1,
  output x2,
  output x3,
  output ovf
);

  wire adder_1_cout, adder_2_cout, adder_3_cout, adder_4_cout;

  Adder #(.width(1)) adder_1 (.a(B0), .b(A0), .out(x0), .cin(1'b0), .cout(adder_1_cout));
  Adder #(.width(1)) adder_2 (.a(B1), .b(A1), .out(x1), .cin(adder_1_cout), .cout(adder_2_cout));
  Adder #(.width(1)) adder_3 (.a(B2), .b(A2), .out(x2), .cin(adder_2_cout), .cout(adder_3_cout));
  Adder #(.width(1)) adder_4 (.a(B3), .b(A3), .out(x3), .cin(adder_3_cout), .cout(adder_4_cout));
  xor xor_1 (ovf, adder_3_cout, adder_4_cout);
endmodule

module Task_1 (
  input  x3,
  input  x2,
  input  x1,
  input  x0,
  output out_5
);

  Multiplexer #(.select(4)) multiplexer_1 (
    .in0(1'b1), .in1(1'b1), .in2(1'b0), .in3(1'b0), .in4(1'b1), .in5(1'b0), .in6(1'b0), .in7(1'b1),
    .in8(1'b0), .in9(1'b0), .in10(1'b0), .in11(1'b0), .in12(1'b1), .in13(1'b0), .in14(1'b0), .in15(1'b1),
    .out(out_5), .sel({x3, x2, x1, x0}));  // open: en

  // Notes on the sheet:
  //   F = { 0,1,4,7,12,15}
endmodule

module Task_2 (
  input  x3,
  input  x2,
  input  x1,
  input  x0,
  output out_5
);

  wire not_1_out, not_2_out;

  not not_1 (not_1_out, x3);
  not not_2 (not_2_out, x3);
  Multiplexer #(.select(3)) multiplexer_1 (
    .in0(not_1_out), .in1(not_2_out), .in2(1'b0), .in3(1'b0), .in4(1'b1), .in5(1'b0), .in6(1'b0), .in7(1'b1),
    .out(out_5), .sel({x2, x1, x0}));  // open: en

  // Notes on the sheet:
  //   F = { 0,1,4,7,12,15}
endmodule

module Task_3 (
  input  x3,
  input  x2,
  input  x1,
  input  x0,
  output out_5
);

  wire nor_1_out, or_1_out;

  or or_1 (or_1_out, ~x3, x2);  // OR_Gate
  nor nor_1 (nor_1_out, x2, x3);
  Multiplexer #(.select(2)) multiplexer_1 (
    .in0(or_1_out), .in1(nor_1_out), .in2(1'b0), .in3(x2), .out(out_5), .sel({x1, x0}));  // open: en

  // Notes on the sheet:
  //   F = { 0,1,4,7,12,15}
endmodule
