// Logisim project SYC_LAB_04_s23239.circ as structural Verilog: 5 circuits, main circuit 4-bit shift register
module _4_bit_shift_register (
  input  in_1,
  input  in_2,
  output out_3
);

  wire clock_1_out, d_ff_1_q, d_ff_2_q, d_ff_3_q;

  Clock clock_1 (.out(clock_1_out));
  D_Flip_Flop d_ff_1 (.clk(clock_1_out), .D(in_1), .Q(d_ff_1_q), .reset(in_2));  // open: Qn, preset, en
  D_Flip_Flop d_ff_2 (.clk(clock_1_out), .D(d_ff_1_q), .Q(d_ff_2_q), .reset(in_2));  // open: Qn, preset, en
  D_Flip_Flop d_ff_3 (.clk(clock_1_out), .D(d_ff_2_q), .Q(d_ff_3_q), .reset(in_2));  // open: Qn, preset, en
  D_Flip_Flop d_ff_4 (.clk(clock_1_out), .D(d_ff_3_q), .Q(out_3), .reset(in_2));  // open: Qn, preset, en
endmodule

module ring_counter (
  input  in_1
);

  wire clock_1_out, d_ff_1_q, d_ff_2_q, d_ff_3_q, d_ff_4_q;

  Clock clock_1 (.out(clock_1_out));
  D_Flip_Flop d_ff_1 (.clk(clock_1_out), .D(d_ff_4_q), .Q(d_ff_1_q), .preset(in_1));  // open: Qn, en, reset
  D_Flip_Flop d_ff_2 (.clk(clock_1_out), .D(d_ff_1_q), .Q(d_ff_2_q));  // open: Qn, preset, en, reset
  D_Flip_Flop d_ff_3 (.clk(clock_1_out), .D(d_ff_2_q), .Q(d_ff_3_q));  // open: Qn, preset, en, reset
  D_Flip_Flop d_ff_4 (.clk(clock_1_out), .D(d_ff_3_q), .Q(d_ff_4_q));  // open: Qn, preset, en, reset
endmodule

module Johnson_counter (
  output out_1
);

  wire clock_1_out, d_ff_1_q, d_ff_2_q, d_ff_3_q;

  Clock clock_1 (.out(clock_1_out));
  D_Flip_Flop d_ff_1 (.clk(clock_1_out), .D(out_1), .Q(d_ff_1_q));  // open: Qn, preset, en, reset
  D_Flip_Flop d_ff_2 (.clk(clock_1_out), .D(d_ff_1_q), .Q(d_ff_2_q));  // open: Qn, preset, en, reset
  D_Flip_Flop d_ff_3 (.clk(clock_1_out), .D(d_ff_2_q), .Q(d_ff_3_q));  // open: Qn, preset, en, reset
  D_Flip_Flop d_ff_4 (.clk(clock_1_out), .D(d_ff_3_q), .Qn(out_1));  // open: Q, preset, en, reset
endmodule

module counter_from_3_to_9 (
);

  wire and_1_out, clock_1_out, d_ff_1_qn, d_ff_2_qn, d_ff_3_qn, d_ff_4_qn;
  wire [3:0] d_ff_1_q;

  Hex_Digit_Display hex_digit_display_1 (.value(d_ff_1_q));  // open: dp
  Clock clock_1 (.out(clock_1_out));
  D_Flip_Flop d_ff_1 (
    .clk(clock_1_out), .D(d_ff_1_qn), .Q(d_ff_1_q[0]), .Qn(d_ff_1_qn), .preset(and_1_out));  // open: en, reset
  and and_1 (and_1_out, d_ff_1_q[3], ~d_ff_1_q[2], d_ff_1_q[1], ~d_ff_1_q[0]);  // AND_Gate
  D_Flip_Flop d_ff_2 (
    .clk(d_ff_1_qn), .D(d_ff_2_qn), .Q(d_ff_1_q[1]), .Qn(d_ff_2_qn), .preset(and_1_out));  // open: en, reset
  D_Flip_Flop d_ff_3 (
    .clk(d_ff_2_qn), .D(d_ff_3_qn), .Q(d_ff_1_q[2]), .Qn(d_ff_3_qn), .reset(and_1_out));  // open: preset, en
  D_Flip_Flop d_ff_4 (
    .clk(d_ff_3_qn), .D(d_ff_4_qn), .Q(d_ff_1_q[3]), .Qn(d_ff_4_qn), .reset(and_1_out));  // open: preset, en
endmodule

module Pseudo_Random_Binary_Signal_generator (
  input  in_1
);

  wire clock_1_out, d_ff_4_q, xor_1_out;
  wire [3:0] d_ff_1_q;

  Hex_Digit_Display hex_digit_display_1 (.value(d_ff_1_q));  // open: dp
  Clock clock_1 (.out(clock_1_out));
  D_Flip_Flop d_ff_1 (.clk(clock_1_out), .D(xor_1_out), .Q(d_ff_1_q[0]), .preset(in_1));  // open: Qn, en, reset
  xor xor_1 (xor_1_out, d_ff_1_q[2], d_ff_4_q);
  D_Flip_Flop d_ff_2 (.clk(clock_1_out), .D(d_ff_1_q[0]), .Q(d_ff_1_q[1]), .preset(in_1));  // open: Qn, en, reset
  D_Flip_Flop d_ff_3 (.clk(clock_1_out), .D(d_ff_1_q[1]), .Q(d_ff_1_q[2]), .preset(in_1));  // open: Qn, en, reset
  D_Flip_Flop d_ff_4 (
    .clk(clock_1_out), .D(d_ff_1_q[2]), .Q(d_ff_4_q), .Qn(d_ff_1_q[3]), .preset(in_1));  // open: en, reset
endmodule
