// Logisim project SYC_LAB_05_s23239.circ as structural Verilog: 2 circuits, main circuit Task1
module Task1 (
  input  in_1
);

  wire and_1_out, and_2_out, and_3_out, and_4_out, and_5_out, and_6_out, and_7_out, clock_1_out, d_ff_1_qn,
       d_ff_2_q, d_ff_2_qn, d_ff_3_q, d_ff_3_qn, or_1_out, or_2_out;

  and and_1 (and_1_out, d_ff_1_qn, d_ff_3_q);
  and and_2 (and_2_out, ~in_1, d_ff_1_qn, d_ff_2_q, d_ff_3_qn);  // AND_Gate
  or or_1 (or_1_out, ~in_1, and_1_out);  // OR_Gate
  and and_3 (and_3_out, in_1, d_ff_2_qn, d_ff_1_qn);
  Clock clock_1 (.out(clock_1_out));
  D_Flip_Flop d_ff_1 (.clk(clock_1_out), .D(and_2_out), .Qn(d_ff_1_qn));  // open: Q, preset, en, reset
  D_Flip_Flop d_ff_2 (.clk(clock_1_out), .D(or_1_out), .Q(d_ff_2_q), .Qn(d_ff_2_qn));  // open: preset, en, reset
  D_Flip_Flop d_ff_3 (.clk(clock_1_out), .D(and_3_out), .Q(d_ff_3_q), .Qn(d_ff_3_qn));  // open: preset, en, reset
  and and_4 (and_4_out, d_ff_1_qn, d_ff_2_qn);
  and and_5 (and_5_out, d_ff_1_qn, d_ff_2_q, d_ff_3_qn);
  and and_6 (and_6_out, d_ff_2_qn, d_ff_3_q, d_ff_1_qn);
  and and_7 (and_7_out, d_ff_1_qn, d_ff_2_q, d_ff_3_q);
  or or_2 (or_2_out, and_5_out, and_6_out);
  LED led_1 (.in(and_4_out));
  LED led_2 (.in(or_2_out));
  LED led_3 (.in(and_7_out));
endmodule

module Task2 (
  input  in_1,
  input  in_2,
  input  in_3
);

  wire and_1_out, and_2_out, and_3_out, and_4_out, and_5_out, and_6_out, and_7_out, and_8_out, and_9_out,
       and_10_out, and_11_out, and_12_out, and_13_out, and_14_out, and_15_out, and_16_out, and_17_out,
       and_18_out, and_19_out, and_20_out, and_21_out, clock_1_out, clock_2_out, clock_3_out, d_ff_1_qn,
       d_ff_2_qn, d_ff_3_q, d_ff_3_qn, d_ff_4_qn, d_ff_5_q, d_ff_5_qn, not_1_out, not_2_out, not_3_out,
       not_4_out, or_1_out, or_2_out, or_3_out, or_4_out, or_5_out, or_6_out, shift_register_1_out,
       shift_register_2_out, shift_register_3_out, shift_register_4_out;

  and and_1 (and_1_out, d_ff_1_qn, shift_register_2_out);
  and and_2 (and_2_out, d_ff_2_qn, shift_register_3_out);
  and and_3 (and_3_out, d_ff_4_qn, d_ff_5_q);
  Clock clock_1 (.out(clock_1_out));
  and and_4 (and_4_out, ~in_1, shift_register_1_out, not_2_out);  // AND_Gate
  or or_1 (or_1_out, ~in_1, and_1_out);  // OR_Gate
  and and_5 (and_5_out, in_1, not_1_out, d_ff_1_qn);
  Clock clock_2 (.out(clock_2_out));
  and and_6 (and_6_out, ~in_2, d_ff_2_qn, d_ff_3_q, not_3_out);  // AND_Gate
  or or_2 (or_2_out, ~in_2, and_2_out);  // OR_Gate
  and and_7 (and_7_out, in_2, d_ff_3_qn, d_ff_2_qn);
  and and_8 (and_8_out, ~in_3, d_ff_4_qn, shift_register_4_out, d_ff_5_qn);  // AND_Gate
  or or_3 (or_3_out, ~in_3, and_3_out);  // OR_Gate
  and and_9 (and_9_out, in_3, not_4_out, d_ff_4_qn);
  D_Flip_Flop d_ff_1 (.clk(clock_1_out), .D(and_4_out), .Qn(d_ff_1_qn));  // open: Q, preset, en, reset
  Shift_Register shift_register_1 (
    .in(or_1_out), .clk(clock_1_out), .out(shift_register_1_out));  // open: shift, load, clr, d0, q0, d1, q1, d2, q2, d3, q3, d4, q4, d5, q5, d6, q6, d7, q7
  Shift_Register shift_register_2 (
    .in(and_5_out), .clk(clock_1_out), .out(shift_register_2_out));  // open: shift, load, clr, d0, q0, d1, q1, d2, q2, d3, q3, d4, q4, d5, q5, d6, q6, d7, q7
  Shift_Register shift_register_3 (
    .in(and_7_out), .clk(clock_2_out), .out(shift_register_3_out));  // open: shift, load, clr, d0, q0, d1, q1, d2, q2, d3, q3, d4, q4, d5, q5, d6, q6, d7, q7
  Clock clock_3 (.out(clock_3_out));
  Shift_Register shift_register_4 (
    .in(or_3_out), .clk(clock_3_out), .out(shift_register_4_out));  // open: shift, load, clr, d0, q0, d1, q1, d2, q2, d3, q3, d4, q4, d5, q5, d6, q6, d7, q7
  D_Flip_Flop d_ff_2 (.clk(clock_2_out), .D(and_6_out), .Qn(d_ff_2_qn));  // open: Q, preset, en, reset
  D_Flip_Flop d_ff_3 (.clk(clock_2_out), .D(or_2_out), .Q(d_ff_3_q), .Qn(d_ff_3_qn));  // open: preset, en, reset
  D_Flip_Flop d_ff_4 (.clk(clock_3_out), .D(and_8_out), .Qn(d_ff_4_qn));  // open: Q, preset, en, reset
  D_Flip_Flop d_ff_5 (.clk(clock_3_out), .D(and_9_out), .Q(d_ff_5_q), .Qn(d_ff_5_qn));  // open: preset, en, reset
  not not_1 (not_1_out, shift_register_1_out);
  not not_2 (not_2_out, shift_register_2_out);
  not not_3 (not_3_out, shift_register_3_out);
  not not_4 (not_4_out, shift_register_4_out);
  and and_10 (and_10_out, d_ff_1_qn, not_1_out);
  and and_11 (and_11_out, d_ff_1_qn, shift_register_1_out, not_2_out);
  and and_12 (and_12_out, not_1_out, shift_register_2_out, d_ff_1_qn);
  and and_13 (and_13_out, d_ff_1_qn, shift_register_1_out, shift_register_2_out);
  or or_4 (or_4_out, and_11_out, and_12_out);
  and and_14 (and_14_out, d_ff_2_qn, d_ff_3_qn);
  and and_15 (and_15_out, d_ff_2_qn, d_ff_3_q, not_3_out);
  or or_5 (or_5_out, and_15_out, and_16_out);
  and and_16 (and_16_out, d_ff_3_qn, shift_register_3_out, d_ff_2_qn);
  and and_17 (and_17_out, d_ff_2_qn, d_ff_3_q, shift_register_3_out);
  and and_18 (and_18_out, d_ff_4_qn, not_4_out);
  and and_19 (and_19_out, d_ff_4_qn, shift_register_4_out, d_ff_5_qn);
  and and_20 (and_20_out, not_4_out, d_ff_5_q, d_ff_4_qn);
  and and_21 (and_21_out, d_ff_4_qn, shift_register_4_out, d_ff_5_q);
  LED led_1 (.in(and_10_out));
  LED led_2 (.in(or_4_out));
  LED led_3 (.in(and_13_out));
  LED led_4 (.in(and_14_out));
  LED led_5 (.in(or_5_out));
  LED led_6 (.in(and_17_out));
  or or_6 (or_6_out, and_19_out, and_20_out);
  LED led_7 (.in(and_18_out));
  LED led_8 (.in(or_6_out));
  LED led_9 (.in(and_21_out));
endmodule
