// Logisim project SYC_Lab_2_s23239.circ as structural Verilog: 4 circuits, main circuit robot
module robot (
  input  F,
  input  L,
  input  R,
  output LW,
  output RW
);

  LWF lwf_1 (.F(F), .R(R), .L(L), .LW(LW));
  RWF rwf_1 (.F(F), .R(R), .L(L), .RW(RW));
endmodule

module LWF (
  input  F,
  input  L,
  input  R,
  output LW
);

  wire nor_1_out, nor_2_out, nor_3_out;

  nor nor_1 (nor_1_out, ~F, L);  // NOR_Gate
  nor nor_2 (nor_2_out, ~F, ~R);  // NOR_Gate
  nor nor_3 (nor_3_out, L, ~R);  // NOR_Gate
  nor nor_4 (LW, nor_1_out, nor_2_out, nor_3_out);
endmodule

module RWF (
  input  F,
  input  L,
  input  R,
  output RW
);

  wire nor_1_out, nor_2_out;

  nor nor_1 (nor_1_out, ~F, ~L);  // NOR_Gate
  nor nor_2 (nor_2_out, ~L, R);  // NOR_Gate
  nor nor_3 (RW, nor_1_out, nor_2_out);
endmodule

module ex1 (
  input  D_2_0,
  input  C_2_1,
  input  x3,
  input  B_2_2,
  input  x2,
  input  x1,
  input  x0,
  input  A_2_3,
  output Y,
  output out_10
);

  wire nand_1_out, nand_2_out, nand_3_out, nand_4_out, nand_6_out, nand_7_out, nand_8_out, nand_9_out,
       nand_10_out, nand_11_out, nand_12_out, nand_13_out, nand_14_out, nand_15_out, nand_16_out,
       nand_17_out, nand_18_out, nand_19_out, nand_20_out, nand_21_out, nand_22_out, nand_23_out,
       nand_24_out, nand_25_out, nand_26_out, nand_27_out, nand_28_out, nand_29_out, nand_30_out,
       nand_31_out, nand_32_out, nand_33_out, nand_34_out, nand_35_out, nand_36_out;

  nand nand_1 (nand_1_out, ~x3, ~x2, ~x1, x0);  // NAND_Gate
  nand nand_2 (nand_2_out, x3, ~x1, ~x0);  // NAND_Gate
  nand nand_3 (nand_3_out, ~x3, x2, x1);  // NAND_Gate
  nand nand_4 (nand_4_out, x2, ~x0);  // NAND_Gate
  nand nand_5 (Y, nand_1_out, nand_2_out, nand_3_out, nand_4_out);
  nand nand_6 (nand_6_out, D_2_0, D_2_0);
  nand nand_7 (nand_7_out, C_2_1, C_2_1);
  nand nand_8 (nand_8_out, B_2_2, B_2_2);
  nand nand_9 (nand_9_out, A_2_3, A_2_3);
  nand nand_10 (nand_10_out, C_2_1, C_2_1);
  nand nand_11 (nand_11_out, B_2_2, B_2_2);
  nand nand_12 (nand_12_out, A_2_3, A_2_3);
  nand nand_13 (nand_13_out, D_2_0, D_2_0);
  nand nand_14 (nand_14_out, C_2_1, C_2_1);
  nand nand_15 (nand_15_out, A_2_3, A_2_3);
  nand nand_16 (nand_16_out, D_2_0, D_2_0);
  nand nand_17 (nand_17_out, C_2_1, C_2_1);
  nand nand_18 (nand_18_out, A_2_3, A_2_3);
  nand nand_19 (nand_19_out, D_2_0, C_2_1, B_2_2, A_2_3);
  nand nand_20 (nand_20_out, nand_6_out, nand_7_out, nand_8_out, nand_9_out);
  nand nand_21 (nand_21_out, D_2_0, nand_10_out, nand_11_out, nand_12_out);
  nand nand_22 (nand_22_out, nand_16_out, nand_17_out, B_2_2, A_2_3);
  nand nand_23 (nand_23_out, D_2_0, C_2_1, B_2_2, nand_18_out);
  nand nand_24 (nand_24_out, nand_19_out, nand_19_out);
  nand nand_25 (nand_25_out, nand_13_out, nand_14_out, B_2_2, nand_15_out);
  nand nand_26 (nand_26_out, nand_20_out, nand_20_out);
  nand nand_27 (nand_27_out, nand_21_out, nand_21_out);
  nand nand_28 (nand_28_out, nand_22_out, nand_22_out);
  nand nand_29 (nand_29_out, nand_23_out, nand_23_out);
  nand nand_30 (nand_30_out, nand_25_out, nand_25_out);
  nand nand_31 (nand_31_out, nand_26_out, nand_26_out);
  nand nand_32 (nand_32_out, nand_27_out, nand_27_out);
  nand nand_33 (nand_33_out, nand_30_out, nand_30_out);
  nand nand_34 (nand_34_out, nand_28_out, nand_28_out);
  nand nand_35 (nand_35_out, nand_29_out, nand_29_out);
  nand nand_36 (nand_36_out, nand_24_out, nand_24_out);
  nand nand_37 (out_10, nand_31_out, nand_32_out, nand_33_out, nand_34_out, nand_35_out, nand_36_out);

  // Notes on the sheet:
  //   F = {1, 4, 6, 7, 8, 12, 14}
  //   0
  //   1
  //   4
  //   12
  //   7
  //   15
endmodule
